// Logisim project ex1-v2.circ as structural Verilog: 1 circuit, main circuit main
module main (
  input  in_1,
  output out_2,
  output out_3,
  output out_4,
  output out_5
);

  wire clock_1_out, d_ff_4_qn, not_1_out, not_2_out, not_3_out, not_4_out;

  Clock clock_1 (.out(clock_1_out));
  D_Flip_Flop d_ff_1 (.clk(clock_1_out), .D(d_ff_4_qn), .Q(out_2), .preset(not_1_out));  // open: Qn, en, reset
  not not_1 (not_1_out, in_1);
  not not_2 (not_2_out, in_1);
  D_Flip_Flop d_ff_2 (.clk(clock_1_out), .D(out_2), .Q(out_3), .reset(not_2_out));  // open: Qn, preset, en
  D_Flip_Flop d_ff_3 (.clk(clock_1_out), .D(out_3), .Q(out_4), .reset(not_3_out));  // open: Qn, preset, en
  not not_3 (not_3_out, in_1);
  D_Flip_Flop d_ff_4 (.clk(clock_1_out), .D(out_4), .Q(out_5), .Qn(d_ff_4_qn), .reset(not_4_out));  // open: preset, en
  not not_4 (not_4_out, in_1);
endmodule
